// Logisim project project2.circ as structural Verilog: 1 circuit, main circuit main
module main (
);

  wire clock_1_out, clock_2_out, decoder_1_out0, decoder_1_out1, decoder_1_out2, decoder_1_out3, Enable;
  wire [1:0] Rm, Rn;
  wire [3:0] X0_q, X0_q_2, X1_q, X1_q_2, X2_q, X2_q_2, X3_q, X3_q_2;
  wire [7:0] adder_1_out, adder_2_out, bit_extender_1_out, DataMemory_dout, imm, multiplexer_1_out,
       multiplexer_2_out, multiplexer_3_out, multiplexer_4_out, multiplexer_5_out, register_1_q,
       subtractor_1_out;
  wire [15:1] InstructionMemory_dout;

  assign bit_extender_1_out = {{7{1'b0}}, Enable};  // Bit_Extender bit_extender_1
  Adder adder_1 (.a(register_1_q), .b(bit_extender_1_out), .out(adder_1_out));  // open: cin, cout
  Register register_1 (.D(adder_1_out), .clk(clock_1_out), .Q(register_1_q));  // open: en, clr
  RAM #(.dataWidth(16), .enables("line")) InstructionMemory (
    .addr(register_1_q), .we(1'b0), .clk(clock_1_out),
    .dout({InstructionMemory_dout[15:11], Rn, Rm, InstructionMemory_dout[6:1], Enable}));  // open: din
  Clock clock_1 (.out(clock_1_out));
  assign imm = {{2{1'b0}}, InstructionMemory_dout[6:1]};  // Bit_Extender bit_extender_2
  Decoder #(.select(2)) decoder_1 (
    .out0(decoder_1_out0), .out1(decoder_1_out1), .out2(decoder_1_out2), .out3(decoder_1_out3),
    .sel(InstructionMemory_dout[12:11]), .en(Enable));
  Register X0 (.D(multiplexer_5_out), .en(decoder_1_out0), .clk(clock_1_out), .Q({X0_q_2, X0_q}));  // open: clr
  Register X1 (.D(multiplexer_5_out), .en(decoder_1_out1), .clk(clock_1_out), .Q({X1_q_2, X1_q}));  // open: clr
  Register X2 (.D(multiplexer_5_out), .en(decoder_1_out2), .clk(clock_1_out), .Q({X2_q_2, X2_q}));  // open: clr
  Register X3 (.D(multiplexer_5_out), .en(decoder_1_out3), .clk(clock_1_out), .Q({X3_q_2, X3_q}));  // open: clr
  Multiplexer #(.select(2), .width(8)) multiplexer_1 (
    .in0({X0_q_2, X0_q}), .in1({X1_q_2, X1_q}), .in2({X2_q_2, X2_q}), .in3({X3_q_2, X3_q}),
    .out(multiplexer_1_out), .sel(Rm));
  Multiplexer #(.select(2), .width(8)) multiplexer_2 (
    .in0({X0_q_2, X0_q}), .in1({X1_q_2, X1_q}), .in2({X2_q_2, X2_q}), .in3({X3_q_2, X3_q}),
    .out(multiplexer_2_out), .sel(Rn));
  Multiplexer #(.width(8)) multiplexer_3 (
    .in0(multiplexer_1_out), .in1(imm), .out(multiplexer_3_out), .sel(InstructionMemory_dout[13]));
  Adder adder_2 (.a(multiplexer_3_out), .b(multiplexer_2_out), .out(adder_2_out));  // open: cin, cout
  Subtractor subtractor_1 (.a(multiplexer_2_out), .b(multiplexer_3_out), .out(subtractor_1_out));  // open: bin, bout
  LED led_1 (.in(clock_2_out));
  LED led_2 (.in(clock_2_out));
  LED led_3 (.in(clock_2_out));
  LED led_4 (.in(clock_2_out));
  LED led_5 (.in(clock_2_out));
  LED led_6 (.in(clock_2_out));
  LED led_7 (.in(clock_2_out));
  LED led_8 (.in(clock_2_out));
  LED led_9 (.in(clock_2_out));
  LED led_10 (.in(clock_2_out));
  LED led_11 (.in(clock_2_out));
  LED led_12 (.in(clock_2_out));
  LED led_13 (.in(clock_2_out));
  LED led_14 (.in(clock_2_out));
  LED led_15 (.in(clock_2_out));
  LED led_16 (.in(clock_2_out));
  LED led_17 (.in(clock_2_out));
  LED led_18 (.in(clock_2_out));
  LED led_19 (.in(clock_2_out));
  LED led_20 (.in(clock_2_out));
  LED led_21 (.in(clock_2_out));
  LED led_22 (.in(clock_2_out));
  LED led_23 (.in(clock_2_out));
  LED led_24 (.in(clock_2_out));
  LED led_25 (.in(clock_2_out));
  LED led_26 (.in(clock_2_out));
  Multiplexer #(.width(8)) multiplexer_4 (
    .in0(adder_2_out), .in1(subtractor_1_out), .out(multiplexer_4_out), .sel(InstructionMemory_dout[15]));
  RAM #(.enables("line")) DataMemory (
    .addr(multiplexer_4_out), .we(1'b0), .clk(clock_2_out), .dout(DataMemory_dout));  // open: din
  Clock clock_2 (.out(clock_2_out));
  LED led_27 (.in(clock_2_out));
  LED led_28 (.in(clock_2_out));
  LED led_29 (.in(clock_2_out));
  LED led_30 (.in(clock_2_out));
  LED led_31 (.in(clock_2_out));
  LED led_32 (.in(clock_2_out));
  LED led_33 (.in(clock_2_out));
  LED led_34 (.in(clock_2_out));
  LED led_35 (.in(clock_2_out));
  LED led_36 (.in(clock_2_out));
  LED led_37 (.in(clock_2_out));
  LED led_38 (.in(clock_2_out));
  LED led_39 (.in(clock_2_out));
  LED led_40 (.in(clock_2_out));
  LED led_41 (.in(clock_2_out));
  LED led_42 (.in(clock_2_out));
  LED led_43 (.in(clock_2_out));
  LED led_44 (.in(clock_2_out));
  LED led_45 (.in(clock_2_out));
  LED led_46 (.in(clock_2_out));
  LED led_47 (.in(clock_2_out));
  // Hex_Digit_Display hex_digit_display_1: pin names not known; wires that end beside it: clock_2_out, clock_2_out
  LED led_48 (.in(clock_2_out));
  Hex_Digit_Display ON_EQUALS_SUS (.dp(clock_2_out));  // open: value
  LED led_49 (.in(clock_2_out));
  LED led_50 (.in(clock_2_out));
  LED led_51 (.in(clock_2_out));
  LED led_52 (.in(clock_2_out));
  LED led_53 (.in(clock_2_out));
  LED led_54 (.in(clock_2_out));
  LED led_55 (.in(clock_2_out));
  LED led_56 (.in(clock_2_out));
  LED led_57 (.in(clock_2_out));
  LED led_58 (.in(clock_2_out));
  LED led_59 (.in(clock_2_out));
  LED led_60 (.in(clock_2_out));
  LED led_61 (.in(clock_2_out));
  LED led_62 (.in(clock_2_out));
  LED led_63 (.in(clock_2_out));
  LED led_64 (.in(clock_2_out));
  LED led_65 (.in(clock_2_out));
  LED led_66 (.in(clock_2_out));
  LED led_67 (.in(clock_2_out));
  LED led_68 (.in(clock_2_out));
  LED led_69 (.in(clock_2_out));
  LED led_70 (.in(clock_2_out));
  LED led_71 (.in(clock_2_out));
  LED led_72 (.in(clock_2_out));
  LED led_73 (.in(clock_2_out));
  LED led_74 (.in(clock_2_out));
  Multiplexer #(.width(8)) multiplexer_5 (
    .in0(multiplexer_4_out), .in1(DataMemory_dout), .out(multiplexer_5_out), .sel(InstructionMemory_dout[14]));
  LED led_75 (.in(clock_2_out));
  LED led_76 (.in(clock_2_out));
  LED led_77 (.in(clock_2_out));
  LED led_78 (.in(clock_2_out));
  LED led_79 (.in(clock_2_out));
  LED led_80 (.in(clock_2_out));
  LED led_81 (.in(clock_2_out));
  Hex_Digit_Display hex_digit_display_2 (.value(X0_q_2));  // open: dp
  Hex_Digit_Display X0_DISPLAY (.value(X0_q));  // open: dp
  Hex_Digit_Display hex_digit_display_3 (.value(X1_q_2));  // open: dp
  Hex_Digit_Display X1_DISPLAY (.value(X1_q));  // open: dp
  Hex_Digit_Display hex_digit_display_4 (.value(X2_q_2));  // open: dp
  Hex_Digit_Display X2_DISPLAY (.value(X2_q));  // open: dp
  Hex_Digit_Display hex_digit_display_5 (.value(X3_q_2));  // open: dp
  Hex_Digit_Display X3_DISPLAY (.value(X3_q));  // open: dp

  // Notes on the sheet:
  //   CPU-Dong: 
  //   Program Counter
  //   the Gentle Beast
  //   Sean Payba and Lili Fortes // I pledge my honor that I have abided by the Stevens Honor System.
  //   equals 0 when adding, 1 when subtracting
  //   enabled when we are loading
  //   enabled when we are using an immediate
endmodule
